# Fritzing sketch shelly-2b-fan-control (saved by Fritzing 0.9.3b)

parts:
  A1 = Shelly plus 2pm
  F1 = Fan - Ventilador [package=THT]
  Composant1 = Lilypad Battery Connect
  S2 = illuminated rocker switch [package=THT]
  S3 = illuminated rocker switch [package=THT]
  S1 = illuminated rocker switch [package=THT]
  F3 = Fan - Ventilador [package=THT]
  LED1 = LEDs [package=led10mm]

nets:
  N1: A1.Pin_8, S1.pin3
  N2: A1.Pin_9, S2.pin3
  N3: A1.Pin_12, Composant1.+, S2.pin1, S1.pin1
  N4: A1.Pin_13, S3.pin1
  N5: A1.Pin_14, Composant1.-, F3.GND
  N6: F1.5V, S3.pin3
  N7: F1.GND, LED1.C
  N8: S3.pin2, F3.5V
  N9: S1.pin2, LED1.A

notes:
  Light on / off
  Speed fast / slow
  Forced march
  Slow fan
  Fast fan
  AC 220V
  Shower light bulb
  Shelly 2PM

custom parts:
  Shelly plus 2pm: Shelly Plus 2PM is a small form factor 2-channel smart switch with power measurement and cover control, which allows remote control of electric appliances through a mobile phone, tablet, PC, or home automation system.
  Fan - Ventilador: Ventilador de 2 pines, se encuentra comunmente en computadoras de escritorio
  illuminated rocker switch: illuminated rocker switch.
  LEDs: LEDs Standard schematic elements and footprints for 5mm, 3mm, 1206, and 0603 sized LEDs. 5mm - Spark Fun Electronics SKU : COM-00529 (and others)
